# Fritzing sketch configuration (saved by Fritzing 0.8.7b)
breadboards: 2

parts:
  LCD1 = LCD screen [part_number=SX09393]
  C1 = Capacitor [package=cap-pth-small2]
  R1 = Rotary Potentiometer (Large) [maximum_resistance=100kΩ package=THT]
  Raspberry_Pi1 = Raspberry Pi B rev1
  IC1 = MCP3008 8-channel 10-bit ADC [part_number=MCP3008]  # not connected
  U1 = 74HC595 [package="DIP16 [THT]"]
  U2 = 74HC595 [package="DIP16 [THT]"]
  U5 = 7-SEGMENT-4DIGIT [package=7-segment-4digit-youngsun]

nets:
  N1: LCD1.E, Raspberry_Pi1.5V
  N2: LCD1.DB0, Raspberry_Pi1.GPIO_14
  GND: LCD1.DB1, C1.2, R1.leg1, U1.GND, U1.OE, U2.GND, U2.OE
  VCC: C1.1, R1.leg2, Raspberry_Pi1.3V3, U1.MR, U1.VCC, U2.MR, U2.VCC
  N3: Raspberry_Pi1.GPIO_17, U1.DS
  N4: Raspberry_Pi1.GPIO_18, U1.SH_CP, U2.SH_CP
  N5: Raspberry_Pi1.GPIO_22, U1.ST_CP, U2.ST_CP
  N6: U1.Q1, U5.16
  N7: U1.Q2, U5.13
  N8: U1.Q3, U5.3
  N9: U1.Q4, U5.5
  N10: U1.Q5, U5.11
  N11: U1.Q6, U5.15
  N12: U1.Q7', U2.DS
  N13: U1.Q0, U5.14
  N14: U2.Q1, U5.2
  N15: U2.Q2, U5.6
  N16: U2.Q3, U5.8
  N17: U2.Q0, U5.1
